# Fritzing sketch no-pcb (saved by Fritzing 0.9.3b)

parts:
  Pusher_Motor = DC Motor
  CPU = Arduino Nano (Rev3.0)
  Flywheel_Switch = Taiway 100-SP-X-T1 SPDT Miniature Toggle Switch [part_number=100-SP-X-T1-0-0-B1-M1 package=THT]
  Trigger_Switch = Taiway 100-SP-X-T1 SPDT Miniature Toggle Switch [part_number=100-SP-X-T1-0-0-B1-M1 package=THT]
  Disconnector_Switch = Taiway 100-SP-X-T1 SPDT Miniature Toggle Switch [part_number=100-SP-X-T1-0-0-B1-M1 package=THT]
  Cycle_Switch = Taiway 100-SP-X-T1 SPDT Miniature Toggle Switch [part_number=100-SP-X-T1-0-0-B1-M1 package=THT]
  Auto_Switch = Taiway 100-SP-X-T1 SPDT Miniature Toggle Switch [part_number=100-SP-X-T1-0-0-B1-M1 package=THT]
  100k = Resistor [tolerance=±5% resistance=100k package=THT]
  1M = Resistor [tolerance=±5% resistance=1M package=THT]
  Battery = Battery block 9V
  4_7k = Resistor [tolerance=±5% resistance=4.7 package=THT]
  Relay = RELAY [package=relay-t9a]

nets:
  N1: Pusher_Motor.pin_1, Relay.MAIN
  N2: Pusher_Motor.pin_2, CPU.GND, 100k.Pin_1, Battery.-, 4_7k.Pin_0, Relay.COIL2, Relay.NC
  N3: CPU.D3, Flywheel_Switch.L1, 4_7k.Pin_1
  N4: CPU.VIN, Trigger_Switch.COM, Cycle_Switch.COM, 1M.Pin_0, Battery.+
  N5: CPU.5V, Flywheel_Switch.COM
  N6: CPU.A0, 100k.Pin_0, 1M.Pin_1
  N7: Trigger_Switch.L1, Disconnector_Switch.COM, Auto_Switch.COM
  N8: Disconnector_Switch.L2, Cycle_Switch.L2, Auto_Switch.L2, Relay.COIL1, Relay.NO
