# Fritzing sketch pcb-v1 (saved by Fritzing 0.9.3b)
circuit board: 4.56888cm x 3.00981cm
perfboards: 1

parts:
  L293D = L293D [package=THT]
  4_7k = Resistor [tolerance=±5% resistance=4.7 package=THT]
  Stepper = female pin header, 4 pins [form="♀ (female)"]
  1M = Resistor [tolerance=±5% resistance=1M package=THT]
  100k = Resistor [tolerance=±5% resistance=100k package=THT]
  11v_In = female pin header, 2 pins [form="♀ (female)"]
  4_7k_2 = Resistor [tolerance=±5% resistance=4.7 package=THT]
  4_7k_3 = Resistor [tolerance=±5% resistance=4.7 package=THT]
  OLED = female pin header, 4 pins [form="♀ (female)"]
  Pot = female pin header, 3 pins [form="♀ (female)"]
  Voltmeter = female pin header, 1 pin [form="♀ (female)"]
  11v_Out = female pin header, 2 pins [form="♀ (female)"]
  11v_Out_2 = female pin header, 2 pins [form="♀ (female)"]
  Step-Power = female pin header, 2 pins [form="♀ (female)"]
  Screen = female pin header, 3 pins [form="♀ (female)"]
  Reload = female pin header, 3 pins [form="♀ (female)"]
  Trigger = female pin header, 3 pins [form="♀ (female)"]
  Step-Control = female pin header, 4 pins [form="♀ (female)"]
  ESCLower = female pin header, 4 pins [form="♀ (female)"]
  OLED_2 = female pin header, 2 pins [form="♀ (female)"]
  Pot_2 = female pin header, 1 pin [form="♀ (female)"]
  ESCUpper = female pin header, 4 pins [form="♀ (female)"]
  5v+ = female pin header, 1 pin [form="♀ (female)"]
  GRN = female pin header, 1 pin [form="♀ (female)"]

nets:
  N1: L293D.Enable_1, L293D.Enable_2, L293D.+V, OLED.pin2, Pot.pin2, Screen.pin3, Reload.pin3, Trigger.pin3, 5v+.pin1
  N2: L293D.In_1, Step-Control.pin1
  N3: L293D.Out_1_(_Controlled_by_Enable_1_), Stepper.pin1
  N4: L293D.0V, 4_7k.Pin_1, 100k.Pin_1, 11v_In.pin2, 4_7k_2.Pin_1, 4_7k_3.Pin_1, OLED.pin1, Pot.pin1, 11v_Out.pin2, 11v_Out_2.pin2, Step-Power.pin1, GRN.pin1
  N5: L293D.Out_2_(_Controlled_by_Enable_1_), Stepper.pin2
  N6: L293D.In_2, Step-Control.pin2
  N7: L293D.+Vmotor, Step-Power.pin2
  N8: L293D.In_3, Step-Control.pin3
  N9: L293D.Out_3_(_Controlled_by_Enable_2_), Stepper.pin3
  N10: L293D.Out_4_(_Controlled_by_Enable_2_), Stepper.pin4
  N11: L293D.In_4, Step-Control.pin4
  N12: 4_7k.Pin_0, Trigger.pin1, Trigger.pin2
  N13: 1M.Pin_0, 100k.Pin_0, Voltmeter.pin1
  N14: 1M.Pin_1, 11v_In.pin1, 11v_Out.pin1, 11v_Out_2.pin1
  N15: 4_7k_2.Pin_0, Reload.pin1, Reload.pin2
  N16: 4_7k_3.Pin_0, Screen.pin1, Screen.pin2
  N17: OLED.pin3, OLED_2.pin1
  N18: OLED.pin4, OLED_2.pin2
  N19: Pot.pin3, Pot_2.pin1
  N20: ESCLower.pin1, ESCLower.pin2
  N21: ESCUpper.pin1, ESCUpper.pin2

notes:
  v5
  v11 In
  Step Out
  Step In
  Volt Meter
  Switches
  OLED
  Pot
  Motors
  v7 Out
  v7 In
  v11 Out
  v5 Ground
