# Fritzing sketch pcb-v2 (saved by Fritzing 0.9.3b)
perfboards: 1

parts:
  Motor_Controller_IC = L293D [package=THT]
  Trigger_Switch_Pull_Down = Resistor [tolerance=±5% resistance=4.7 package=THT]
  Stepper_Control = female pin header, 4 pins [form="♀ (female)"]
  Volt_In = Resistor [tolerance=±5% resistance=1M package=THT]
  Volt_Out = Resistor [tolerance=±5% resistance=100k package=THT]
  Reload_Switch_Pull_Dowm = Resistor [tolerance=±5% resistance=4.7 package=THT]
  Display_Switch_Pull_Down = Resistor [tolerance=±5% resistance=4.7 package=THT]
  OLED_Connector = female pin header, 4 pins [form="♀ (female)"]
  Pot_Connector = female pin header, 3 pins [form="♀ (female)"]
  5v_Out = female pin header, 2 pins [form="♀ (female)"]
  11v_Out = female pin header, 2 pins [form="♀ (female)"]
  5v_In = female pin header, 2 pins [form="♀ (female)"]
  Arduino = Arduino Nano (Rev3.0)
  Motor_Lower = female pin header, 3 pins [form="♀ (female)"]
  Motor_Upper = female pin header, 3 pins [form="♀ (female)"]
  11v_Out1 = female pin header, 2 pins [form="♀ (female)"]
  11v_Out2 = female pin header, 2 pins [form="♀ (female)"]
  11v_Out3 = female pin header, 2 pins [form="♀ (female)"]

nets:
  N1: Motor_Controller_IC.Enable_1, Motor_Controller_IC.Enable_2, Motor_Controller_IC.+V, OLED_Connector.pin2, Pot_Connector.pin2, Arduino.5V, 11v_Out1.pin1, 11v_Out2.pin1, 11v_Out3.pin1
  N2: Motor_Controller_IC.In_1, Arduino.D3
  N3: Motor_Controller_IC.Out_1_(_Controlled_by_Enable_1_), Stepper_Control.pin1
  N4: Motor_Controller_IC.0V, Trigger_Switch_Pull_Down.Pin_1, Volt_Out.Pin_1, Reload_Switch_Pull_Dowm.Pin_1, Display_Switch_Pull_Down.Pin_1, OLED_Connector.pin1, Pot_Connector.pin1, 5v_Out.pin2, 11v_Out.pin2, 5v_In.pin1, Arduino.GND
  N5: Motor_Controller_IC.Out_2_(_Controlled_by_Enable_1_), Stepper_Control.pin2
  N6: Motor_Controller_IC.In_2, Arduino.D4
  N7: Motor_Controller_IC.+Vmotor, 5v_In.pin2
  N8: Motor_Controller_IC.In_3, Arduino.D5
  N9: Motor_Controller_IC.Out_3_(_Controlled_by_Enable_2_), Stepper_Control.pin3
  N10: Motor_Controller_IC.Out_4_(_Controlled_by_Enable_2_), Stepper_Control.pin4
  N11: Motor_Controller_IC.In_4, Arduino.D6
  N12: Trigger_Switch_Pull_Down.Pin_0, Arduino.D11/MOSI, 11v_Out3.pin2
  N13: Volt_In.Pin_0, Volt_Out.Pin_0, Arduino.A2
  N14: Volt_In.Pin_1, 5v_Out.pin1, 11v_Out.pin1, Arduino.VIN
  N15: Reload_Switch_Pull_Dowm.Pin_0, Arduino.D10, 11v_Out2.pin2
  N16: Display_Switch_Pull_Down.Pin_0, Arduino.D9, 11v_Out1.pin2
  N17: OLED_Connector.pin3, Arduino.A5
  N18: OLED_Connector.pin4, Arduino.A4
  N19: Pot_Connector.pin3, Arduino.A3
  N20: Arduino.D7, Motor_Lower.pin1
  N21: Arduino.D8, Motor_Upper.pin1
