# Fritzing sketch pcb-v3 (saved by Fritzing 0.9.3b)
perfboards: 1

parts:
  100k1 = Resistor [tolerance=±5% resistance=100k package=THT]
  1M1 = Resistor [tolerance=±5% resistance=1M package=THT]
  4_7k3 = Resistor [tolerance=±5% resistance=4.7 package=THT]
  Bat2 = female pin header, 2 pins [form="♀ (female)"]
  4_7k4 = Resistor [tolerance=±5% resistance=4.7 package=THT]
  4_7k5 = Resistor [tolerance=±5% resistance=4.7 package=THT]
  Screen2 = female pin header, 2 pins [form="♀ (female)"]
  Screen3 = female pin header, 2 pins [form="♀ (female)"]
  Screen4 = female pin header, 2 pins [form="♀ (female)"]
  Screen5 = female pin header, 2 pins [form="♀ (female)"]
  4_7k6 = Resistor [tolerance=±5% resistance=4.7 package=THT]
  ESC_Upper2 = female pin header, 3 pins [form="♀ (female)"]
  ESC_Upper3 = female pin header, 3 pins [form="♀ (female)"]
  OLED2 = female pin header, 4 pins [form="♀ (female)"]
  Pot2 = female pin header, 3 pins [form="♀ (female)"]
  D2 = Rectifier Diode [part_number=1N4001 package="300 mil [THT]"]
  R2 = Resistor [tolerance=±5% resistance=270 package="0402 [SMD]"]
  U2 = TRANSISTOR_NPN_2 [package=to-92]
  Bat3 = female pin header, 2 pins [form="♀ (female)"]
  Part2 = Arduino Nano (Rev3.0)

nets:
  N1: 100k1.Pin_0, 1M1.Pin_0, Part2.A6
  N2: 4_7k3.Pin_0, Screen2.pin2, Part2.D12/MISO
  N3: 4_7k3.Pin_1, 4_7k5.Pin_1
  N4: Bat2.pin1, 4_7k4.Pin_1, 4_7k6.Pin_1, OLED2.pin2, Pot2.pin2, U2.C
  N5: Bat2.pin2, Bat3.pin2
  N6: 4_7k4.Pin_0, Screen3.pin2, Part2.D11/MOSI
  N7: 4_7k5.Pin_0, Screen4.pin2, Part2.D10
  N8: Screen2.pin1, Screen3.pin1, Screen4.pin1, Screen5.pin1, OLED2.pin1, Pot2.pin1, Part2.5V
  N9: Screen5.pin2, 4_7k6.Pin_0, Part2.D9
  N10: ESC_Upper2.pin1, Part2.D7
  N11: ESC_Upper3.pin1, Part2.D8
  N12: OLED2.pin3, Part2.A4
  N13: OLED2.pin4, Part2.A5
  N14: Pot2.pin3, Part2.A7
  N15: D2.anode, U2.E, Bat3.pin1
  N16: R2.Pin_0, Part2.D6
  N17: R2.Pin_1, U2.B
