# Fritzing sketch pcb (saved by Fritzing 0.9.3b)
circuit board: 4.56888cm x 3.00981cm
perfboards: 1

parts:
  Motor_Controller_IC = L293D [package=THT]
  Trigger_Switch_Pull_Down = Resistor [tolerance=±5% resistance=4.7 package=THT]
  Stepper_Control = female pin header, 4 pins [form="♀ (female)"]
  Volt_In = Resistor [tolerance=±5% resistance=1M package=THT]
  Volt_Out = Resistor [tolerance=±5% resistance=100k package=THT]
  11v_In = female pin header, 2 pins [form="♀ (female)"]
  Reload_Switch_Pull_Dowm = Resistor [tolerance=±5% resistance=4.7 package=THT]
  Display_Switch_Pull_Down = Resistor [tolerance=±5% resistance=4.7 package=THT]
  OLED_Connector = female pin header, 4 pins [form="♀ (female)"]
  Pot_Connector = female pin header, 3 pins [form="♀ (female)"]
  Voltmeter = female pin header, 1 pin [form="♀ (female)"]
  5v_Out = female pin header, 2 pins [form="♀ (female)"]
  11v_Out = female pin header, 2 pins [form="♀ (female)"]
  5v_In = female pin header, 2 pins [form="♀ (female)"]
  Display_Switch = female pin header, 3 pins [form="♀ (female)"]
  Reload_Switch = female pin header, 3 pins [form="♀ (female)"]
  Trigger_Switch = female pin header, 3 pins [form="♀ (female)"]
  Stepper_Motor = female pin header, 4 pins [form="♀ (female)"]
  Motor_Lower = female pin header, 4 pins [form="♀ (female)"]
  OLED_Control = female pin header, 2 pins [form="♀ (female)"]
  Pot_Signal = female pin header, 1 pin [form="♀ (female)"]
  Motor_Upper = female pin header, 4 pins [form="♀ (female)"]
  5v_+ = female pin header, 1 pin [form="♀ (female)"]
  5v_- = female pin header, 1 pin [form="♀ (female)"]

nets:
  N1: Motor_Controller_IC.Enable_1, Motor_Controller_IC.Enable_2, Motor_Controller_IC.+V, OLED_Connector.pin2, Pot_Connector.pin2, Display_Switch.pin3, Reload_Switch.pin3, Trigger_Switch.pin3, 5v_+.pin1
  N2: Motor_Controller_IC.In_1, Stepper_Motor.pin1
  N3: Motor_Controller_IC.Out_1_(_Controlled_by_Enable_1_), Stepper_Control.pin1
  N4: Motor_Controller_IC.0V, Trigger_Switch_Pull_Down.Pin_1, Volt_Out.Pin_1, 11v_In.pin2, Reload_Switch_Pull_Dowm.Pin_1, Display_Switch_Pull_Down.Pin_1, OLED_Connector.pin1, Pot_Connector.pin1, 5v_Out.pin2, 11v_Out.pin2, 5v_In.pin1, 5v_-.pin1
  N5: Motor_Controller_IC.Out_2_(_Controlled_by_Enable_1_), Stepper_Control.pin2
  N6: Motor_Controller_IC.In_2, Stepper_Motor.pin2
  N7: Motor_Controller_IC.+Vmotor, 5v_In.pin2
  N8: Motor_Controller_IC.In_3, Stepper_Motor.pin3
  N9: Motor_Controller_IC.Out_3_(_Controlled_by_Enable_2_), Stepper_Control.pin3
  N10: Motor_Controller_IC.Out_4_(_Controlled_by_Enable_2_), Stepper_Control.pin4
  N11: Motor_Controller_IC.In_4, Stepper_Motor.pin4
  N12: Trigger_Switch_Pull_Down.Pin_0, Trigger_Switch.pin1, Trigger_Switch.pin2
  N13: Volt_In.Pin_0, Volt_Out.Pin_0, Voltmeter.pin1
  N14: Volt_In.Pin_1, 11v_In.pin1, 5v_Out.pin1, 11v_Out.pin1
  N15: Reload_Switch_Pull_Dowm.Pin_0, Reload_Switch.pin1, Reload_Switch.pin2
  N16: Display_Switch_Pull_Down.Pin_0, Display_Switch.pin1, Display_Switch.pin2
  N17: OLED_Connector.pin3, OLED_Control.pin1
  N18: OLED_Connector.pin4, OLED_Control.pin2
  N19: Pot_Connector.pin3, Pot_Signal.pin1
  N20: Motor_Lower.pin1, Motor_Lower.pin2
  N21: Motor_Upper.pin1, Motor_Upper.pin2

notes:
  v5
  v11 In
  Step Out
  Step In
  Volt Meter
  Switches
  OLED
  Pot
  Motors
  v7 Out
  v7 In
  v11 Out
  v5 Ground
