# Fritzing sketch wiring (saved by Fritzing 0.9.3b)
breadboards: 1

parts:
  IC2 = L293D [package=THT]
  M1 = Stepper Motor - Bipolar
  Part1 = Arduino Micro (Rev3)
  Grove1 = Grove OLED 128x96
  J1 = Dagu DGServo 9g header connector (female) [package=THT]
  J2 = Dagu DGServo 9g header connector (female) [package=THT]
  S1 = Toggle Switch [package=THT]
  R1 = Rotary Potentiometer (Small) [maximum_resistance=100kΩ package=THT]
  S2 = Toggle Switch [package=THT]
  S3 = Toggle Switch [package=THT]
  S4 = Toggle Switch [package=THT]
  R5 = Resistor [tolerance=±5% resistance=4.7 package=THT]
  R6 = Resistor [tolerance=±5% resistance=4.7 package=THT]
  R7 = Resistor [tolerance=±5% resistance=4.7 package=THT]
  R8 = Resistor [tolerance=±5% resistance=4.7 package=THT]
  LM1 = RioRand LM2596
  LM2 = RioRand LM2596

nets:
  N1: IC2.Enable_1, IC2.+Vmotor, Grove1.VCC, S1.L2, S2.L2, S3.L2, S4.COM, S4.L2, LM2.Pin_2
  N2: IC2.In_1, M1.D, Part1.D3/SCL
  N3: IC2.0V, Part1.D9_PWM/A9, Part1.D10_PWM/A10, Part1.D11_PWM, Part1.D12_PWM/A11, Grove1.GND, R1.leg2, R5.Pin_0, R6.Pin_0, R7.Pin_0, R8.Pin_0, LM1.Pin_3, LM2.Pin_3
  N4: IC2.Out_2_(_Controlled_by_Enable_1_), M1.B
  N5: IC2.In_2, Part1.D4_PWM/A6
  N6: IC2.Enable_2, IC2.+V, R1.leg1, LM1.Pin_2
  N7: IC2.In_3, Part1.D5_PWM
  N8: IC2.Out_3_(_Controlled_by_Enable_2_), M1.C
  N9: IC2.Out_4_(_Controlled_by_Enable_2_), Part1.D6_PWM/A7
  N10: IC2.In_4, M1.A
  N11: Part1.D7, J2.gnd
  N12: Part1.D8_PWM/A8, J1.gnd
  N13: Part1.A5, Grove1.SCL
  N14: Part1.A4, Grove1.SDA
  N15: Part1.A3, R1.wiper
  N16: S1.L1, S1.COM, R5.Pin_1
  N17: S2.L1, S2.COM, R6.Pin_1
  N18: S3.L1, S3.COM, R7.Pin_1
  N19: S4.L1, R8.Pin_1
